# Fritzing sketch Master (saved by Fritzing 0.9.3b)
stripboards: 1

parts:
  J1 = female pin header, 8 pins [form="♀ (female)"]
  J5 = female pin header, 4 pins [form="♀ (female)"]
  J4 = female pin header, 3 pins [form="♀ (female)"]
  J2 = female pin header, 7 pins [form="♀ (female)"]
  T1 = LM35 Temperature Sensor [package="TO92 [THT]"]

nets:
  N1: J1.pin6, J4.pin2, T1.Vout, T1.GND
  N2: J5.pin3, J2.pin4
  N3: J5.pin4, J4.pin1, J2.pin1, T1.+Vs
  N4: J4.pin3, J2.pin5
